# Fritzing sketch morseCodeTransmitter (saved by Fritzing 0.9.6b)
breadboards: 1

parts:
  LED1 = LEDs [package=led10mm]
  Buzzer = Piezo Speaker
  R1 = Resistor [tolerance=±5% resistance=220 package="0603 [SMD]"]
  S1 = Square Pushbutton
  R2 = Resistor [tolerance=±5% resistance=220 package="0603 [SMD]"]
  Morse_Code_Transmitter = Arduino Uno (Rev3) - ICSP

nets:
  N1: LED1.C, R1.Pin_0
  N2: LED1.A, Morse_Code_Transmitter.D13/SCK
  N3: Buzzer.pin1, Morse_Code_Transmitter.A1
  N4: Buzzer.pin2, R1.Pin_1, R2.Pin_1, Morse_Code_Transmitter.GND
  N5: S1.leg0, R2.Pin_0, Morse_Code_Transmitter.A0
  N6: S1.leg1, Morse_Code_Transmitter.5V
